# Fritzing sketch Montage (saved by Fritzing 0.9.9b)
breadboards: 1

parts:
  part = Resistor [tolerance=±5% resistance=220 package=THT]
  part_2 = Resistor [tolerance=±5% resistance=220 package=THT]
  LED1 = LED - 5mm [color="Orange (605nm)" package="5 mm [THT]"]
  LED2 = LED - 5mm [color="Green (565nm)" package="5 mm [THT]"]
  LED3 = LED - 5mm [color="Red (633nm)" package="5 mm [THT]"]
  LED4 = RGB LED (com. cathode, rgb) [package="5 mm [THT]"]
  part_3 = Resistor [tolerance=±5% resistance=220 package=THT]
  part_4 = Resistor [tolerance=±5% resistance=220 package=THT]
  part_5 = Resistor [tolerance=±5% resistance=220 package=THT]
  Composant1 = Arduino Uno (Rev3)
  Composant2 = LCD1602-I2C
  U1 = NodeMCU V1.0
  YwRobot_Power_Supply1 = YwRobot Breadboard Power Supply [part_number=545043]

nets:
  N1: part.Pin_0, LED4.green_anode
  N2: part.Pin_1, Composant1.D11_PWM/MOSI
  N3: part_2.Pin_0, LED4.red_anode
  N4: part_2.Pin_1, Composant1.D10_PWM/SS
  GND: LED1.cathode, LED2.cathode, LED3.cathode, LED4.common_cathode, Composant1.GND, Composant2.GND, U1.GND, YwRobot_Power_Supply1.GND
  N5: LED1.anode, part_3.Pin_0
  N6: LED2.anode, part_4.Pin_0
  N7: LED3.anode, part_5.Pin_0
  N8: part_3.Pin_1, Composant1.D4
  N9: part_4.Pin_1, Composant1.D3_PWM
  N10: part_5.Pin_1, Composant1.D2
  N11: Composant1.A4/SDA, Composant2.SDA
  N12: Composant1.A5/SCL, Composant2.SCL
  N13: Composant1.D0/RX, U1.D4
  VIN: Composant1.VIN, Composant2.VCC, U1.Vin, YwRobot_Power_Supply1.VCC

custom parts:
  LCD1602-I2C: A standard character display, usually with 2x16 characters. Comes in many colors with LCM1602 IIC attached.
  NodeMCU V1.0: ESP8266 based NodeMCU
  YwRobot Breadboard Power Supply: The YwRobot Breadboard Power Supply (MB-V2) has two power rails; they can be 5V or 3V3. Power to the module can be provided through the female USB socket or through the A10 (female) 2.1mm power jack.
